# Fritzing sketch concepto conexionado (saved by Fritzing 0.9.0b)
stripboards: 2

parts:
  J4 = male pin header, 8 pins [form="♂ (male)"]
  Conector_de_5V_GND_Vin = male pin header, 3 pins [form="♂ (male)"]
  R2 = Resistor [tolerance=±5% resistance=1.5k package="1206 [SMD]"]
  S1 = Toggle Switch [package=THT]
  U1 = LIPO-2000mAh [package=lipo-2000]
  EB_I4_I3 = female pin header, 3 pins [form="♀ (female)"]
  EA_I2_I1 = female pin header, 3 pins [form="♀ (female)"]
  J11 = male pin header, 1 pin [form="♂ (male)"]
  J12 = male pin header, 1 pin [form="♂ (male)"]
  J13 = male pin header, 1 pin [form="♂ (male)"]
  J14 = male pin header, 1 pin [form="♂ (male)"]
  Sensores_motor_A = male pin header, 2 pins [form="♂ (male)"]
  Sensores_motor_B = male pin header, 2 pins [form="♂ (male)"]
  CNY70 = mystery part, 4 pins [chip_label=?]
  CNY70_2 = mystery part, 4 pins [chip_label=?]
  +5V_GND = female pin header, 2 pins [form="♀ (female)"]
  Conector_Motor_A/Driver = Screw terminal - 2 pins [package=THT]
  Conector_Motor_B/Driver = Screw terminal - 2 pins [package=THT]
  J6 = male pin header, 8 pins [form="♂ (male)"]
  J15 = male pin header, 8 pins [form="♂ (male)"]
  J16 = male pin header, 8 pins [form="♂ (male)"]  # not connected
  J17 = male pin header, 18 pins [form="♂ (male)"]
  J18 = male pin header, 18 pins [form="♂ (male)"]
  XOR_TC4030BP = IC, DIP package, 14 pins [chip_label=IC]
  J21 = male pin header, 8 pins [form="♂ (male)"]
  J22 = male pin header, 6 pins [form="♂ (male)"]
  Parte2 = Arduino Mega 2560 (Rev3)  # not connected
  J30 = female pin header, 4 pins [form="♀ (female)"]
  J31 = female pin header, 4 pins [form="♀ (female)"]
  J28 = female pin header, 4 pins [form="♀ (female)"]
  J29 = female pin header, 4 pins [form="♀ (female)"]
  J32 = male pin header, 4 pins [form="♂ (male)"]
  J26 = female pin header, 4 pins [form="♀ (female)"]
  C3 = Electrolytic Capacitor [capacitance=10µF package="100 mil [THT, electrolytic]"]
  R3 = Resistor [tolerance=±5% resistance=12k package=THT]
  R5 = Resistor [tolerance=±5% resistance=15k package=THT]
  LED2 = RGB LED (com. cathode, rgb) [package="5 mm [THT]"]
  J33 = Piezo Speaker

nets:
  N1: J4.pin1, EB_I4_I3.pin3
  N2: J4.pin3, Sensores_motor_A.pin1, XOR_TC4030BP.pin6
  N3: J4.pin4, Sensores_motor_A.pin2, XOR_TC4030BP.pin5
  N4: J4.pin5, XOR_TC4030BP.pin4
  N5: J4.pin6, XOR_TC4030BP.pin3
  N6: J4.pin7, Sensores_motor_B.pin1, XOR_TC4030BP.pin2
  N7: J4.pin8, Sensores_motor_B.pin2, XOR_TC4030BP.pin1
  N8: Conector_de_5V_GND_Vin.pin1, S1.COM, J22.pin6, R3.Pin_0
  N9: Conector_de_5V_GND_Vin.pin2, +5V_GND.pin2, J22.pin4, R5.Pin_0
  N10: Conector_de_5V_GND_Vin.pin3, +5V_GND.pin1, XOR_TC4030BP.pin14, J22.pin3
  N11: R2.Pin_1, U1.-, J22.pin5
  N12: S1.L2, U1.+
  N13: EB_I4_I3.pin1, J21.pin7
  N14: EB_I4_I3.pin2, J21.pin8
  N15: EA_I2_I1.pin1, J21.pin5
  N16: EA_I2_I1.pin2, J21.pin4
  N17: EA_I2_I1.pin3, J21.pin3
  N18: J11.pin1, Conector_Motor_B/Driver.pin2
  N19: J12.pin1, Conector_Motor_A/Driver.pin2
  N20: J13.pin1, Conector_Motor_B/Driver.pin1
  N21: J14.pin1, Conector_Motor_A/Driver.pin1
  N22: CNY70.pin1, CNY70.pin2, J6.pin6
  N23: CNY70_2.pin1, J6.pin5
  N24: J6.pin1, R3.Pin_1, R5.Pin_1
  N25: J15.pin8, J26.pin1
  N26: J17.pin1, J18.pin1
  N27: J17.pin13, LED2.green_anode
  N28: J17.pin18, J18.pin18, LED2.common_cathode
  N29: J18.pin13, LED2.red_anode
  N30: J18.pin14, LED2.blue_anode
  N31: XOR_TC4030BP.pin7, J21.pin2, J33.pin1
  N32: J21.pin6, J33.pin2
  N33: J22.pin2, J26.pin4
  N34: J30.pin1, J32.pin4
  N35: J30.pin2, J29.pin3
  N36: J30.pin3, J29.pin2
  N37: J30.pin4, J32.pin1, C3.+
  N38: J31.pin1, J28.pin3, J32.pin3
  N39: J31.pin2, J28.pin2, J32.pin2
  N40: J31.pin3, J29.pin4
  N41: J31.pin4, J28.pin1, J29.pin1, C3.-
